// Logisim project Cicuito para o Quarto.circ as structural Verilog: 1 circuit, main circuit main
module main (
  input  p,
  input  q,
  output out_3
);

  wire and_1_out, not_1_out, or_1_out;

  and and_1 (and_1_out, p, q);
  not not_1 (not_1_out, p);
  or or_1 (or_1_out, not_1_out, and_1_out);
  and and_2 (out_3, p, or_1_out);
endmodule
