// Logisim project Circuito para a Sala e a Cozinha.circ as structural Verilog: 1 circuit, main circuit main
module main (
  input  a,
  input  b,
  input  c,
  output out_4
);

  wire and_1_out, and_2_out, and_3_out, not_1_out, not_2_out, or_1_out;

  not not_1 (not_1_out, a);
  not not_2 (not_2_out, b);
  and and_1 (and_1_out, not_1_out, b);
  and and_2 (and_2_out, not_1_out, not_2_out, c);
  or or_1 (or_1_out, a, and_1_out);
  and and_3 (and_3_out, or_1_out, b);
  or or_2 (out_4, and_3_out, and_2_out);
endmodule
