// Logisim project Circuito para a Área Externa.circ as structural Verilog: 1 circuit, main circuit main
module main (
  input  a,
  input  b,
  input  c,
  input  d,
  output out_5
);

  wire and_1_out, or_1_out, or_2_out;

  or or_1 (or_1_out, a, b);
  and and_1 (and_1_out, b, d);
  or or_2 (or_2_out, c, and_1_out);
  and and_2 (out_5, or_1_out, or_2_out);
endmodule
